// Logisim project ALUAdderTest.circ as structural Verilog: 1 circuit, main circuit main
module main (
);

  wire and_1_out, and_2_out, CarryIn_out, not_1_out, not_2_out, or_1_out, or_2_out, or_3_out, or_4_out,
       xor_1_out, xor_2_out, xor_3_out, XY_sw1, XY_sw2;

  DipSwitch #(.number(2)) XY (.sw1(XY_sw1), .sw2(XY_sw2));
  and and_1 (and_1_out, XY_sw2, XY_sw1);
  Button CarryIn (.out(CarryIn_out));
  xor xor_1 (xor_1_out, XY_sw1, XY_sw2);
  xor xor_2 (xor_2_out, CarryIn_out, xor_1_out);
  and and_2 (and_2_out, xor_1_out, CarryIn_out);
  xor xor_3 (xor_3_out, and_2_out, and_1_out);
  _7_Segment_Display u_7_segment_display_1 (
    .f(not_1_out), .a(not_1_out), .b(or_1_out), .e(not_1_out), .d(not_1_out), .c(or_2_out));  // open: g, dp
  not not_1 (not_1_out, xor_2_out);
  _7_Segment_Display u_7_segment_display_2 (
    .f(not_2_out), .a(not_2_out), .b(or_3_out), .e(not_2_out), .d(not_2_out), .c(or_4_out));  // open: g, dp
  not not_2 (not_2_out, xor_3_out);
  or or_1 (or_1_out, xor_2_out, not_1_out);
  or or_2 (or_2_out, not_1_out, xor_2_out);
  or or_3 (or_3_out, xor_3_out, not_2_out);
  or or_4 (or_4_out, not_2_out, xor_3_out);

  // Notes on the sheet:
  //   Sum
  //   CarryOut
endmodule
